# Fritzing sketch tpFinal (saved by Fritzing 1.0.6)
breadboards: 1

parts:
  Componente1 = Arduino Mega 2560 (Rev3)
  S1 = Pushbutton [package="[THT]"]
  S2 = Pushbutton [package="[THT]"]
  Componente3 = HW-080 Soil Moisture Sensor
  Componente4 = HW-080 Soil moisture sensor - controler
  Grove1 = Grove RGB LCD
  U1 = ESP8266 WiFi Module [part_number=ESP8266]
  A1 = ESP01S Adaptor [package="DIP (Dual Inline) [THT]"]
  KF-1 = KF-301 Relay [package=THT]
  WATER_PUMP1 = water pump/motor
  VCC3 = 4 x AAA Battery Mount [internal_resistance=0.1Ω]

nets:
  N1: Componente1.A0, Componente4.AO
  N2: Componente1.D21/SCL, Componente1.SCL, Grove1.SCL
  N3: Componente1.D20/SDA, Componente1.SDA, Grove1.SDA
  GND: Componente1.GND, S1.Pin_3, S1.Pin_4, S2.Pin_3, S2.Pin_4, Componente4.GND, Grove1.GND, A1.GND#3, KF-1.ground
  N4: Componente1.D10_PWM, S1.Pin_1, S1.Pin_2
  N5: Componente1.D8_PWM, S2.Pin_1, S2.Pin_2
  VCC: Componente1.5V, Componente4.VCC, Grove1.VCC, A1.VCC, KF-1.power
  N6: Componente1.D2_PWM, KF-1.signal
  N7: Componente1.D3_PWM, A1.RX#0
  N8: Componente1.D4_PWM, A1.TX
  N9: Componente3.POS, Componente4.POS
  N10: Componente3.NEG, Componente4.NEG
  N11: U1.RXD, A1.RX#8
  N12: U1.GPIO_0, A1.IO0
  N13: U1.GPIO_2, A1.IO2
  N14: U1.GND, A1.GND#11
  N15: KF-1.C, VCC3.+
  N16: KF-1.NO, WATER_PUMP1.pin_2
  N17: WATER_PUMP1.pin_1, VCC3.-

custom parts:
  ESP8266 WiFi Module: Generic WiFi Module based on the ESP8266 with onboard PCB antenna and UART communications
  ESP01S Adaptor: Please ignore the PCB view — it's not supposed to be there.
  KF-301 Relay: KF-301
  water pump/motor: WATER PUMP BY ARDUBLOCKTR
